// Logisim project 4bitALU.circ as structural Verilog: 5 circuits, main circuit FullAdder
module main (
  input  in_1,
  input  CONTROL,
  input  in_3,
  input  in_4,
  input  in_5,
  input  INPUT_A,
  input  in_7,
  input  in_8,
  input  in_9,
  input  INPUT_B,
  input  in_11,
  output out_12,
  output OUTPUT,
  output out_14,
  output out_15,
  output out_16,
  output out_17,
  output out_18,
  output out_19
);

  ALU alu_1 (
    .CS2(in_1), .CS1(CONTROL), .CS0(in_3), .A0(in_4), .A1(in_5), .A2(INPUT_A), .A3(in_7), .B0(in_8),
    .B1(in_9), .B2(INPUT_B), .B3(in_11), .F0(out_12), .F1(OUTPUT), .F2(out_14), .F3(out_15), .Z_FLAG(out_16),
    .S_FLAG(out_17), .C_FLAG(out_18), .V_FLAG(out_19));

  // Notes on the sheet:
  //   4 BIT ALU
  //   STATUS FLAGS
endmodule

module FullAdder (
  input  A,
  input  B,
  input  Cin,
  output SUM,
  output Carry_Out
);

  wire and_1_out, and_2_out, xor_1_out;

  xor xor_1 (xor_1_out, A, B);
  and and_1 (and_1_out, Cin, xor_1_out);
  and and_2 (and_2_out, A, B);
  xor xor_2 (SUM, xor_1_out, Cin);
  or or_1 (Carry_Out, and_1_out, and_2_out);
endmodule

module CombinationalCircuit (
  input  CS2,
  input  CS1,
  input  CS0,
  input  a0,
  input  a1,
  input  a2,
  input  a3,
  input  b0,
  input  b1,
  input  in_10,
  input  b3,
  output x0,
  output x1,
  output x2,
  output x3,
  output y0,
  output y1,
  output y2,
  output y3,
  output CS0_2,
  output CS1_2
);

  wire and_1_out, and_2_out, and_3_out, and_4_out, and_5_out, and_6_out, and_7_out, and_8_out, and_9_out,
       not_1_out, not_2_out, not_3_out, not_4_out, not_5_out;

  not not_1 (not_1_out, CS2);
  not not_2 (not_2_out, b0);
  not not_3 (not_3_out, b1);
  not not_4 (not_4_out, in_10);
  not not_5 (not_5_out, b3);
  and and_1 (and_1_out, CS2, CS0);
  and and_2 (and_2_out, not_1_out, b0);
  and and_3 (and_3_out, not_1_out, b1);
  and and_4 (and_4_out, not_1_out, in_10);
  and and_5 (and_5_out, not_1_out, b3);
  and and_6 (and_6_out, and_1_out, not_2_out);
  and and_7 (and_7_out, and_1_out, not_3_out);
  and and_8 (and_8_out, and_1_out, not_4_out);
  and and_9 (and_9_out, and_1_out, not_5_out);
  or or_1 (x0, a0, and_6_out);
  or or_2 (x1, a1, and_7_out);
  or or_3 (x2, a2, and_8_out);
  or or_4 (x3, a3, and_9_out);
  or or_5 (y0, and_6_out, and_2_out);
  or or_6 (y1, and_7_out, and_3_out);
  or or_7 (y2, and_8_out, and_4_out);
  or or_8 (y3, and_9_out, and_5_out);

  assign CS0_2 = CS0;
  assign CS1_2 = CS1;

  // Notes on the sheet:
  //   b2
endmodule

module N_BIT_PARALLEL_ADDER (
  input  X0,
  input  X1,
  input  in_3,
  input  X3,
  input  Y0,
  input  Y1,
  input  Y2,
  input  Y3,
  input  CS0,
  input  CS1,
  output F0,
  output F1,
  output F2,
  output F3,
  output out_15,
  output out_16
);

  wire and_1_out, and_2_out, and_3_out, fulladder_1_carry_out, fulladder_2_carry_out, fulladder_3_carry_out,
       not_1_out;

  not not_1 (not_1_out, CS0);
  and and_1 (and_1_out, not_1_out, CS1);
  and and_2 (and_2_out, fulladder_1_carry_out, not_1_out);
  and and_3 (and_3_out, fulladder_2_carry_out, not_1_out);
  and and_4 (out_15, fulladder_3_carry_out, not_1_out);
  FullAdder fulladder_1 (.A(X0), .B(Y0), .Cin(and_1_out), .SUM(F0), .Carry_Out(fulladder_1_carry_out));
  FullAdder fulladder_2 (.A(X1), .B(Y1), .Cin(and_2_out), .SUM(F1), .Carry_Out(fulladder_2_carry_out));
  FullAdder fulladder_3 (.A(in_3), .B(Y2), .Cin(and_3_out), .SUM(F2), .Carry_Out(fulladder_3_carry_out));
  FullAdder fulladder_4 (.A(X3), .B(Y3), .Cin(out_15), .SUM(F3), .Carry_Out(out_16));

  // Notes on the sheet:
  //   X2
  //   FA0
  //   FA1
  //   FA2
  //   FA3
  //   FA2 CARRY OUT
  //   FA3 CARRY OUT
endmodule

module ALU (
  input  CS2,
  input  CS1,
  input  CS0,
  input  A0,
  input  A1,
  input  A2,
  input  A3,
  input  B0,
  input  B1,
  input  B2,
  input  B3,
  output F0,
  output F1,
  output F2,
  output F3,
  output Z_FLAG,
  output S_FLAG,
  output C_FLAG,
  output V_FLAG
);

  wire combinationalcircuit_1_cs0_2, combinationalcircuit_1_cs1_2, combinationalcircuit_1_x0,
       combinationalcircuit_1_x1, combinationalcircuit_1_x2, combinationalcircuit_1_x3,
       combinationalcircuit_1_y0, combinationalcircuit_1_y1, combinationalcircuit_1_y2,
       combinationalcircuit_1_y3, n_bit_parallel_adder_1_out_15;

  CombinationalCircuit combinationalcircuit_1 (
    .CS2(CS2), .CS1(CS1), .CS0(CS0), .a0(A0), .a1(A1), .a2(A2), .a3(A3), .b0(B0), .b1(B1), .in_10(B2),
    .b3(B3), .x0(combinationalcircuit_1_x0), .x1(combinationalcircuit_1_x1), .x2(combinationalcircuit_1_x2),
    .x3(combinationalcircuit_1_x3), .y0(combinationalcircuit_1_y0), .y1(combinationalcircuit_1_y1),
    .y2(combinationalcircuit_1_y2), .y3(combinationalcircuit_1_y3), .CS0_2(combinationalcircuit_1_cs0_2),
    .CS1_2(combinationalcircuit_1_cs1_2));
  N_BIT_PARALLEL_ADDER n_bit_parallel_adder_1 (
    .X0(combinationalcircuit_1_x0), .X1(combinationalcircuit_1_x1), .in_3(combinationalcircuit_1_x2),
    .X3(combinationalcircuit_1_x3), .Y0(combinationalcircuit_1_y0), .Y1(combinationalcircuit_1_y1),
    .Y2(combinationalcircuit_1_y2), .Y3(combinationalcircuit_1_y3), .F0(F0), .F1(F1), .F2(F2), .F3(F3),
    .out_16(C_FLAG), .out_15(n_bit_parallel_adder_1_out_15), .CS0(combinationalcircuit_1_cs0_2),
    .CS1(combinationalcircuit_1_cs1_2));
  nor nor_1 (Z_FLAG, F3, F2, F1, F0);
  xor xor_1 (V_FLAG, n_bit_parallel_adder_1_out_15, C_FLAG);

  assign S_FLAG = F3;

  // Notes on the sheet:
  //   Z FLAG
  //   S FLAG
  //    C FLAG
  //   V FLAG
endmodule
