// Logisim project v1.circ as structural Verilog: 5 circuits, main circuit main
module main (
  output out_1,
  output [19:0] INSTRUCTION,
  output [7:0] rd1,
  output [7:0] WD,
  output [7:0] rd2,
  output [7:0] t0,
  output [7:0] t1,
  output [7:0] t2,
  output [7:0] t3,
  output [7:0] t4,
  output [7:0] t5,
  output [7:0] zero,
  output [7:0] sp
);

  wire alu_1_out_4, and_1_out, and_2_out, clock_1_out, control_unit_1_alu_src, control_unit_1_branch,
       control_unit_1_branch_n, control_unit_1_jmp, control_unit_1_mem_2_reg, control_unit_1_mem_read,
       control_unit_1_mem_write, control_unit_1_reg_dest, control_unit_1_reg_write, control_unit_1_shift,
       not_1_out, or_1_out;
  wire [2:0] control_unit_1_alu_op_0;
  wire [3:0] multiplexer_1_out;
  wire [7:0] adder_1_out, adder_2_out, alu_1_f, data_memory_1_read_data, multiplexer_2_out,
       multiplexer_3_out, multiplexer_4_out, multiplexer_5_out, multiplexer_7_out, PC_q;

  Register PC (.D(multiplexer_7_out), .Q(PC_q), .clk(clock_1_out));  // open: en, clr
  Adder adder_1 (.a(PC_q), .b(8'h1), .out(adder_1_out), .cin(1'b0));  // open: cout
  Clock clock_1 (.out(clock_1_out));
  ROM #(.dataWidth(20)) rom_1 (.addr(PC_q), .data(INSTRUCTION));  // open: sel
  Multiplexer #(.width(4), .enable("false")) multiplexer_1 (
    .in0(INSTRUCTION[11:8]), .in1(INSTRUCTION[7:4]), .out(multiplexer_1_out), .sel(control_unit_1_reg_dest));
  Multiplexer #(.width(8), .enable("false")) multiplexer_2 (
    .in0(INSTRUCTION[7:0]), .in1({4'b0000, INSTRUCTION[3:0]}), .out(multiplexer_2_out),
    .sel(control_unit_1_shift));
  Control_Unit control_unit_1 (
    .INSTRUCTION(INSTRUCTION[19:16]), .ALU_OP_0(control_unit_1_alu_op_0[0]),
    .ALU_OP_1(control_unit_1_alu_op_0[1]), .ALU_OP_2(control_unit_1_alu_op_0[2]), .JMP(control_unit_1_jmp),
    .BRANCH(control_unit_1_branch), .MEM_WRITE(control_unit_1_mem_write), .MEM_READ(control_unit_1_mem_read),
    .REG_WRITE(control_unit_1_reg_write), .MEM_2_REG(control_unit_1_mem_2_reg),
    .ALU_SRC(control_unit_1_alu_src), .REG_DEST(control_unit_1_reg_dest), .SHIFT(control_unit_1_shift),
    .Branch_N(control_unit_1_branch_n));
  Registers registers_1 (
    .READ_REGISTER_1(INSTRUCTION[15:12]), .READ_REGISTER_2(INSTRUCTION[11:8]),
    .WRITE_REGISTER(multiplexer_1_out), .WRITE_DATA(WD), .REG_WRITE(control_unit_1_reg_write),
    .READ_DATA_1(rd1), .READ_DATA_2(rd2), .CLK(clock_1_out), .t0(t0), .t1(t1), .t2(t2), .t3(t3), .t4(t4),
    .zero(zero), .sp(sp), .t5(t5));
  Multiplexer #(.width(8), .enable("false")) multiplexer_3 (
    .in0(rd1), .in1(rd2), .out(multiplexer_3_out), .sel(control_unit_1_shift));
  Multiplexer #(.width(8), .enable("false")) multiplexer_4 (
    .in0(rd2), .in1(multiplexer_2_out), .out(multiplexer_4_out), .sel(control_unit_1_alu_src));
  ALU alu_1 (
    .A(multiplexer_3_out), .B(multiplexer_4_out), .ALUop(control_unit_1_alu_op_0), .ZF(out_1), .F(alu_1_f),
    .out_4(alu_1_out_4));  // open: out_5
  Adder adder_2 (.a(adder_1_out), .b(INSTRUCTION[7:0]), .out(adder_2_out), .cin(1'b0));  // open: cout
  not not_1 (not_1_out, out_1);
  and and_1 (and_1_out, control_unit_1_branch, out_1);
  or or_1 (or_1_out, and_1_out, and_2_out);
  and and_2 (and_2_out, control_unit_1_branch_n, not_1_out);
  Data_Memory data_memory_1 (
    .WRITE_DATA(rd2), .MEM_WRITE(control_unit_1_mem_write), .ADDRESS(alu_1_f), .CLK(clock_1_out),
    .READ_DATA(data_memory_1_read_data), .MEM_READ(control_unit_1_mem_read));
  Multiplexer #(.width(8), .enable("false")) multiplexer_5 (
    .in0(adder_1_out), .in1(adder_2_out), .out(multiplexer_5_out), .sel(or_1_out));
  Multiplexer #(.width(8), .enable("false")) multiplexer_6 (
    .in0(alu_1_f), .in1(data_memory_1_read_data), .out(WD), .sel(control_unit_1_mem_2_reg));
  Multiplexer #(.width(8), .enable("false")) multiplexer_7 (
    .in0(multiplexer_5_out), .in1(INSTRUCTION[15:8]), .out(multiplexer_7_out), .sel(control_unit_1_jmp));

  // Notes on the sheet:
  //   READ ADDRESS
  //   contents of rom_1 (hex, n*v repeats v):
  //   f56ff f510a d6100 b6601 f6601 a6100 c1340 e4210 d6200 b6601 f540f a1103 8012a b0105 10130 d6400
  //   b6601 d6300 b6601 f6601 a6000 1600 d6000 b6601 f6601 a6100 3021a d6200 b6601 d6700 b6601 90301 3400
  //   2200 30042 c4310 21040 e4310 41100 71014 d0002 a1106 8011c 3100 1500 2e00 d6300 b6601 3400 3200
  //   934fa 534ed 3500 41100 71014 d0002 3900 e3130
  //   to shift
  //   adder
endmodule

module ALU (
  input  [7:0] A,
  input  [7:0] B,
  input  [2:0] ALUop,
  output out_4,
  output out_5,
  output ZF,
  output [7:0] F
);

  wire [7:0] adder_1_out, and_1_out, nor_1_out, or_1_out, subtractor_1_out;
  wire [15:0] shifter_1_out, shifter_2_out;

  Adder adder_1 (.a(A), .b(B), .out(adder_1_out), .cin(1'b0), .cout(out_4));
  Subtractor subtractor_1 (.a(A), .b(B), .out(subtractor_1_out), .bin(1'b0), .bout(out_5));
  assign or_1_out = A | B;  // OR_Gate or_1, 8 bits wide
  assign and_1_out = A & B;  // AND_Gate and_1, 8 bits wide
  assign nor_1_out = ~(A | B);  // NOR_Gate nor_1, 8 bits wide
  Shifter #(.width(16)) shifter_1 (.in({{8{1'b0}}, A}), .\dist (B[3:0]), .out(shifter_1_out));
  Shifter #(.width(16), .shift("lr")) shifter_2 (.in({{8{1'b0}}, A}), .\dist (B[3:0]), .out(shifter_2_out));
  Multiplexer #(.select(3), .width(8), .enable("false")) multiplexer_1 (
    .in0(adder_1_out), .in1(subtractor_1_out), .in2(or_1_out), .in3(and_1_out), .in4(nor_1_out),
    .in5(shifter_1_out[7:0]), .in6(shifter_2_out[7:0]), .in7({8{1'b0}}), .out(F), .sel(ALUop));
  nor nor_2 (ZF, F[0], F[1], F[2], F[3], F[4], F[5], F[6], F[7]);
endmodule

module Registers (
  input  [3:0] READ_REGISTER_1,
  input  [3:0] READ_REGISTER_2,
  input  [3:0] WRITE_REGISTER,
  input  [7:0] WRITE_DATA,
  input  CLK,
  input  REG_WRITE,
  output [7:0] t0,
  output [7:0] t1,
  output [7:0] t2,
  output [7:0] READ_DATA_1,
  output [7:0] t3,
  output [7:0] t4,
  output [7:0] zero,
  output [7:0] sp,
  output [7:0] t5,
  output [7:0] READ_DATA_2
);

  wire demultiplexer_1_out0, demultiplexer_1_out1, demultiplexer_1_out2, demultiplexer_1_out3,
       demultiplexer_1_out4, demultiplexer_1_out5, demultiplexer_1_out6, demultiplexer_1_out7;

  Demultiplexer #(.select(4), .disabled(0)) demultiplexer_1 (
    .out0(demultiplexer_1_out0), .out1(demultiplexer_1_out1), .out2(demultiplexer_1_out2),
    .out3(demultiplexer_1_out3), .out4(demultiplexer_1_out4), .out5(demultiplexer_1_out5),
    .out6(demultiplexer_1_out6), .out7(demultiplexer_1_out7), .in(1'b1), .sel(WRITE_REGISTER), .en(REG_WRITE));  // open: out8, out9, out10, out11, out12, out13, out14, out15
  Register u_t0 (.D(WRITE_DATA), .en(demultiplexer_1_out0), .Q(t0), .clk(CLK));  // open: clr
  Register u_t1 (.D(WRITE_DATA), .en(demultiplexer_1_out1), .Q(t1), .clk(CLK));  // open: clr
  Register u_t2 (.D(WRITE_DATA), .en(demultiplexer_1_out2), .Q(t2), .clk(CLK));  // open: clr
  Register u_t3 (.D(WRITE_DATA), .en(demultiplexer_1_out3), .Q(t3), .clk(CLK));  // open: clr
  Register u_t4 (.D(WRITE_DATA), .en(demultiplexer_1_out4), .Q(t4), .clk(CLK));  // open: clr
  Register u_ZERO (.D(WRITE_DATA), .en(demultiplexer_1_out5), .Q(zero));  // open: clk, clr
  Register u_SP (.D(WRITE_DATA), .en(demultiplexer_1_out6), .Q(sp), .clk(CLK));  // open: clr
  Register u_t5 (.D(WRITE_DATA), .en(demultiplexer_1_out7), .Q(t5), .clk(CLK));  // open: clr
  Multiplexer #(.select(4), .width(8), .enable("false")) multiplexer_1 (
    .in0(t0), .in1(t1), .in2(t2), .in3(t3), .in4(t4), .in5(zero), .in6(sp), .in7(t5), .out(READ_DATA_1),
    .sel(READ_REGISTER_1));  // open: in8, in9, in10, in11, in12, in13, in14, in15
  Multiplexer #(.select(4), .width(8), .enable("false")) multiplexer_2 (
    .in0(t0), .in1(t1), .in2(t2), .in3(t3), .in4(t4), .in5(zero), .in6(sp), .in7(t5), .out(READ_DATA_2),
    .sel(READ_REGISTER_2));  // open: in8, in9, in10, in11, in12, in13, in14, in15
endmodule

module Data_Memory (
  input  [7:0] ADDRESS,
  input  [7:0] WRITE_DATA,
  input  MEM_WRITE,
  input  MEM_READ,
  input  CLK,
  output [7:0] READ_DATA
);

  RAM #(.bus("separate")) ram_1 (
    .addr(ADDRESS), .din(WRITE_DATA), .data(READ_DATA), .str(MEM_WRITE), .clk(CLK), .ld(MEM_READ));  // open: sel, clr

  // Notes on the sheet:
  //   DATA MEMORY
endmodule

module Control_Unit (
  input  [3:0] INSTRUCTION,
  output ALU_OP_0,
  output ALU_OP_1,
  output ALU_OP_2,
  output JMP,
  output BRANCH,
  output MEM_WRITE,
  output MEM_READ,
  output REG_WRITE,
  output MEM_2_REG,
  output ALU_SRC,
  output REG_DEST,
  output SHIFT,
  output Branch_N
);

  wire [15:15] rom_1_data;

  ROM #(.addrWidth(4), .dataWidth(16)) rom_1 (
    .addr(INSTRUCTION),
    .data({{3{rom_1_data[15]}}, Branch_N, SHIFT, REG_DEST, ALU_SRC, MEM_2_REG, REG_WRITE, MEM_READ, MEM_WRITE, BRANCH, JMP, ALU_OP_2, ALU_OP_1, ALU_OP_0}));  // open: sel
  // also tied to GND on the sheet: rom_1_data[15]

  // Notes on the sheet:
  //   contents of rom_1 (hex, n*v repeats v):
  //   71f 480 482 e85 283 1501 483 282 e86 511 3c0 281 481 720 484 280
endmodule
