// Logisim project ckt21.circ as structural Verilog: 4 circuits, main circuit main
module main (
  input  [15:0] in_1,
  input  [15:0] in_2,
  output [11:0] out_3,
  output [11:0] out_4,
  output [12:0] out_5,
  output [12:0] out_6,
  output [12:0] out_7,
  output [12:0] out_8,
  output [12:0] out_9,
  output [13:0] out_10,
  output out_11,
  output out_12,
  output out_13,
  output out_14,
  output out_15,
  output out_16,
  output out_17,
  output out_18,
  output out_19,
  output out_20,
  output out_21,
  output out_22,
  output out_23,
  output out_24,
  output out_25,
  output out_26,
  output out_27,
  output [3:0] out_28,
  output UNDERFLOW,
  output [4:0] out_30,
  output out_31,
  output [13:0] out_32,
  output [12:0] out_33,
  output OVERFLOW,
  output out_35,
  output out_36,
  output [3:0] out_37,
  output [4:0] out_38,
  output [4:0] out_39,
  output [12:0] out_40,
  output a__b,
  output [3:0] out_42
);

  wire comparator_1_eq, comparator_1_gt, comparator_2_eq, comparator_2_gt, comparator_3_eq, comparator_3_gt,
       not_1_out, not_2_out, or_3_out, or_5_out;
  wire [3:0] subtractor_1_out;
  wire [11:11] or_1_out, or_2_out;
  wire [12:0] adder_1_out, shifter_2_out, shifter_3_out;

  or or_1 (or_1_out[11], in_2[11], in_2[12], in_2[13], in_2[14]);
  or or_2 (or_2_out[11], in_1[11], in_1[12], in_1[13], in_1[14]);
  Subtractor #(.width(4)) subtractor_1 (
    .a(in_1[14:11]), .b(in_2[14:11]), .out(subtractor_1_out), .bin(1'b0), .bout(out_31));
  Comparator #(.width(4), .mode("unsigned")) comparator_1 (
    .a(in_1[14:11]), .b(in_2[14:11]), .gt(comparator_1_gt), .eq(comparator_1_eq), .lt(a__b));
  or or_3 (or_3_out, comparator_1_gt, comparator_1_eq);
  _4bit_twos_complement u_4bit_twos_complement_1 (
    ._0(subtractor_1_out[0]), ._1(subtractor_1_out[1]), ._2(subtractor_1_out[2]), ._3(subtractor_1_out[3]),
    .b_out(out_31), .out_6(out_28));
  Multiplexer #(.width(4), .enable("false")) multiplexer_1 (
    .in0(in_2[14:11]), .in1(in_1[14:11]), .out(out_38[3:0]), .sel(or_3_out));
  not not_1 (not_1_out, out_31);
  Multiplexer #(.width(13), .disabled(0), .enable("false")) multiplexer_2 (
    .in0({in_1[15], or_2_out[11], in_1[10:0]}), .in1({in_2[15], or_1_out[11], in_2[10:0]}),
    .out({out_6[12], out_3}), .sel(not_1_out));
  Multiplexer #(.width(13), .enable("false")) multiplexer_3 (
    .in0({in_1[15], or_2_out[11], in_1[10:0]}), .in1({in_2[15], or_1_out[11], in_2[10:0]}), .out(out_40),
    .sel(out_31));
  Shifter #(.width(12), .shift("lr")) shifter_1 (.in(out_3), .\dist (out_28), .out(out_4));
  _13bit_twos_complement u_13bit_twos_complement_1 (
    .in_1({1'b0, out_40[11:0]}), .in_2(out_40[12]), .out_3({out_32[13], out_32[11:0]}));  // open: out_4
  _13bit_twos_complement u_13bit_twos_complement_2 (
    .in_1({1'b0, out_4}), .in_2(out_6[12]), .out_3(out_8));  // open: out_4
  Adder #(.width(14)) adder_1 (
    .a({{2{out_8[12]}}, out_8[11:0]}), .b({{2{out_32[13]}}, out_32[11:0]}), .out({out_22, adder_1_out}),
    .cin(1'b0), .cout(out_27));
  _13bit_twos_complement u_13bit_twos_complement_3 (.in_1(adder_1_out), .in_2(out_22), .out_3(out_7));  // open: out_4
  priority_encoder priority_encoder_1 (
    ._03(out_39[3]), ._02(out_39[2]), ._01(out_39[1]), .O0(out_39[0]), ._0(out_7[0]), ._1(out_7[1]),
    ._2(out_7[2]), ._3(out_7[3]), ._4(out_7[4]), ._5(out_7[5]), ._6(out_7[6]), ._7(out_7[7]), ._8(out_7[8]),
    ._9(out_7[9]), ._10(out_7[10]), ._11(out_7[11]), ._12(out_7[12]), .O4(out_39[4]));
  _4bit_twos_complement u_4bit_twos_complement_2 (
    ._0(out_39[0]), ._1(out_39[1]), ._2(out_39[2]), ._3(out_39[3]), .b_out(out_39[4]), .out_6(out_37));
  Subtractor #(.width(5)) subtractor_2 (
    .a({1'b0, out_38[3:0]}), .b(out_39), .out({out_30[4], out_23, out_24, out_25, out_26}), .bin(1'b0),
    .bout(out_36));
  Shifter #(.width(13)) shifter_2 (.in(out_7), .\dist (out_37), .out(shifter_2_out));
  Shifter #(.width(13), .shift("lr")) shifter_3 (.in(out_7), .\dist (out_37), .out(shifter_3_out));
  Comparator #(.width(5)) comparator_2 (
    .a({5{1'b0}}), .b({out_30[4], out_23, out_24, out_25, out_26}), .gt(comparator_2_gt), .eq(comparator_2_eq));  // open: lt
  Comparator #(.width(5), .mode("unsigned")) comparator_3 (
    .a({out_30[4], out_23, out_24, out_25, out_26}), .b(5'b01111), .gt(comparator_3_gt), .eq(comparator_3_eq));  // open: lt
  Multiplexer #(.width(13), .enable("false")) multiplexer_4 (
    .in0(shifter_2_out), .in1(shifter_3_out), .out(out_9), .sel(out_39[4]));
  or or_4 (UNDERFLOW, comparator_2_gt, comparator_2_eq);
  or or_5 (or_5_out, comparator_3_gt, comparator_3_eq);
  not not_2 (not_2_out, UNDERFLOW);
  and and_1 (OVERFLOW, not_2_out, or_5_out);

  assign out_5 = {1'b0, out_4};
  assign out_6[11:0] = out_3;
  assign out_10 = {{2{out_8[12]}}, out_8[11:0]};
  assign out_11 = out_9[10];
  assign out_12 = out_9[9];
  assign out_13 = out_9[8];
  assign out_14 = out_9[7];
  assign out_15 = out_9[6];
  assign out_16 = out_9[5];
  assign out_17 = out_9[4];
  assign out_18 = out_9[3];
  assign out_19 = out_9[2];
  assign out_20 = out_9[1];
  assign out_21 = out_9[0];
  assign out_30[3:0] = {out_23, out_24, out_25, out_26};
  assign out_32[12] = out_32[13];
  assign out_33 = {out_32[13], out_32[11:0]};
  assign out_35 = out_22;
  assign out_38[4] = 1'b0;
  assign out_42 = out_38[3:0];

  // Notes on the sheet:
  //   A
  //   B
  //   LSB
  //   MSB
  //   LSB
  //   MSB
  //   if bout = 1 , a< b 
  //   Emax = 7
  //   Emin = -6
  //   bias = 7
  //   subtractor
  //   a
  //   b
  //   input A
  //   implicit 1
  //   input B
  //   smaller out
  //   bigger or equal out
  //   12 bit shifter
  //   14 bit adder
  //   FP ADDER sign bit
  //   0
  //   15
  //   FP ADDER OUTPUT
endmodule

module _4bit_twos_complement (
  input  _0,
  input  _1,
  input  _2,
  input  _3,
  input  b_out,
  output [3:0] out_6
);

  wire [3:0] xor_1_out;

  xor xor_1 (xor_1_out[0], _0, b_out);
  xor xor_2 (xor_1_out[1], _1, b_out);
  xor xor_3 (xor_1_out[2], _2, b_out);
  xor xor_4 (xor_1_out[3], _3, b_out);
  Adder #(.width(4)) adder_1 (.a(xor_1_out), .b(4'b0000), .out(out_6), .cin(b_out));  // open: cout
endmodule

module _13bit_twos_complement (
  input  [12:0] in_1,
  input  in_2,
  output [12:0] out_3,
  output out_4
);

  wire [12:0] xor_1_out;

  xor xor_1 (xor_1_out[0], in_1[0], in_2);
  xor xor_2 (xor_1_out[1], in_1[1], in_2);
  xor xor_3 (xor_1_out[2], in_1[2], in_2);
  xor xor_4 (xor_1_out[3], in_1[3], in_2);
  xor xor_5 (xor_1_out[4], in_1[4], in_2);
  xor xor_6 (xor_1_out[5], in_1[5], in_2);
  xor xor_7 (xor_1_out[6], in_1[6], in_2);
  xor xor_8 (xor_1_out[7], in_1[7], in_2);
  xor xor_9 (xor_1_out[8], in_1[8], in_2);
  xor xor_10 (xor_1_out[9], in_1[9], in_2);
  xor xor_11 (xor_1_out[10], in_1[10], in_2);
  xor xor_12 (xor_1_out[11], in_1[11], in_2);
  xor xor_13 (xor_1_out[12], in_1[12], in_2);
  Adder #(.width(13)) adder_1 (.a(xor_1_out), .b({13{1'b0}}), .out(out_3), .cin(in_2), .cout(out_4));
endmodule

module priority_encoder (
  input  _0,
  input  _1,
  input  _2,
  input  _3,
  input  _4,
  input  _5,
  input  _6,
  input  _7,
  input  _8,
  input  _9,
  input  _10,
  input  _11,
  input  _12,
  output O4,
  output _03,
  output _02,
  output _01,
  output O0
);

  wire and_1_out, and_2_out, and_3_out, and_4_out, and_5_out, and_6_out, and_7_out, and_8_out, and_9_out,
       and_10_out, and_11_out, and_12_out, and_13_out, and_14_out, and_15_out, and_16_out, and_17_out,
       and_18_out, and_19_out, and_20_out, and_21_out, and_22_out, and_23_out, and_24_out, and_25_out,
       and_26_out, and_27_out, not_1_out, not_2_out, not_3_out, not_4_out, not_5_out, not_6_out, not_7_out,
       not_8_out, not_9_out, not_10_out, not_11_out, not_12_out, or_1_out, or_2_out, or_3_out, or_4_out,
       or_5_out, or_6_out, or_9_out;

  not not_1 (not_1_out, _1);
  not not_2 (not_2_out, _2);
  not not_3 (not_3_out, _3);
  not not_4 (not_4_out, _4);
  not not_5 (not_5_out, _5);
  not not_6 (not_6_out, _6);
  not not_7 (not_7_out, _7);
  not not_8 (not_8_out, _9);
  not not_9 (not_9_out, _8);
  not not_10 (not_10_out, _10);
  not not_11 (not_11_out, _11);
  not not_12 (not_12_out, _12);
  and and_1 (and_1_out, not_12_out, not_11_out, not_10_out, not_8_out, not_9_out, not_7_out, not_6_out, not_5_out, not_4_out);
  and and_2 (and_2_out, not_3_out, _2);
  and and_3 (and_3_out, not_3_out, not_2_out, _1);
  and and_4 (and_4_out, not_3_out, not_2_out, not_1_out, _0);
  and and_5 (and_5_out, not_9_out, not_7_out, _6);
  and and_6 (and_6_out, not_4_out, not_3_out, _2);
  and and_7 (and_7_out, not_4_out, not_3_out, _0, not_2_out, not_1_out);
  or or_1 (or_1_out, _3, and_2_out, and_3_out, and_4_out);
  and and_8 (and_8_out, not_12_out, not_11_out, not_10_out, not_8_out, not_9_out);
  and and_9 (and_9_out, not_7_out, _6);
  and and_10 (and_10_out, not_7_out, not_6_out, _5);
  and and_11 (and_11_out, not_7_out, not_6_out, not_5_out, _4);
  and and_12 (and_12_out, not_12_out, not_11_out, not_10_out);
  and and_13 (and_13_out, not_8_out, _8);
  and and_14 (and_14_out, not_12_out, not_11_out, _10);
  and and_15 (and_15_out, not_12_out, not_11_out, not_10_out, not_8_out);
  or or_2 (or_2_out, _8, and_5_out);
  or or_3 (or_3_out, _7, and_9_out, and_10_out, and_11_out);
  or or_4 (or_4_out, _9, and_13_out);
  and and_16 (and_16_out, and_12_out, not_8_out, not_9_out, not_7_out, not_6_out);
  and and_17 (and_17_out, not_5_out, _4);
  and and_18 (and_18_out, and_15_out, or_2_out);
  and and_19 (and_19_out, and_15_out, not_9_out, not_7_out, not_6_out, not_5_out);
  or or_5 (or_5_out, _4, and_6_out, and_7_out);
  and and_20 (and_20_out, and_1_out, or_1_out);
  and and_21 (and_21_out, and_8_out, or_3_out);
  and and_22 (and_22_out, and_12_out, or_4_out);
  or or_6 (or_6_out, _5, and_17_out);
  and and_23 (and_23_out, and_19_out, or_5_out);
  or or_7 (_03, _12, and_20_out);
  or or_8 (_02, _12, and_21_out);
  and and_24 (and_24_out, and_16_out, not_5_out, not_4_out, not_3_out, not_2_out);
  and and_25 (and_25_out, not_1_out, _0);
  and and_26 (and_26_out, and_16_out, or_6_out);
  or or_9 (or_9_out, _1, and_25_out);
  and and_27 (and_27_out, and_24_out, or_9_out);
  or or_10 (O0, _12, and_14_out, and_18_out, and_23_out);
  or or_11 (_01, _12, and_22_out, and_26_out, and_27_out);

  assign O4 = _12;
endmodule
