// Logisim project v1-12.circ as structural Verilog: 10 circuits, main circuit main
module main (
  input  RESET_PC,
  input  Reg_Write_Manual,
  input  [3:0] WRITE_REG_ADDRESS_MANUAL,
  input  [7:0] WRITE_REGISTER_DATA,
  output [3:0] WR,
  output [3:0] WR_2,
  output [7:0] alu2,
  output [7:0] alu3,
  output [19:0] INSTRUCTION,
  output out_10,
  output [7:0] t0,
  output [7:0] t1,
  output [7:0] t2,
  output [7:0] t3,
  output [7:0] alu1,
  output [7:0] t4,
  output [7:0] t5,
  output [7:0] A,
  output [7:0] B,
  output [7:0] zero,
  output [7:0] sp,
  output [3:0] WR_3,
  output [7:0] WD
);

  wire clock_1_out, control_unit_1_mem_read, control_unit_1_mem_write, ex_mem_1_mr_2, ex_mem_1_mw_2,
       ex_mem_1_rw_2, id_ex_1_mr_2, id_ex_1_mw_2, MAIN_CLK_out, mem_wb_1_rw_2, multiplexer_1_out,
       multiplexer_4_out;
  wire [1:0] forwarding_unit_1_fd_a, forwarding_unit_1_fd_b;
  wire [3:0] control_unit_1_alu_op_0, id_ex_1_cntrl_out, id_ex_1_rd_2, id_ex_1_rs_2, id_ex_1_wr_2,
       if_id_1_output_2;
  wire [7:0] adder_1_out, data_memory_1_read_data, ex_mem_1_rd2_2, id_ex_1_rd1_2, id_ex_1_rd1_3, PC_q,
       registers_1_read_data_1, registers_1_read_data_2;
  wire [19:0] if_id_1_output;

  Register PC (.D(adder_1_out), .Q(PC_q), .clk(MAIN_CLK_out), .clr(RESET_PC));  // open: en
  Adder adder_1 (.a(PC_q), .b(8'h1), .out(adder_1_out), .cin(1'b0));  // open: cout
  ROM #(.dataWidth(20)) rom_1 (.addr(PC_q), .data(INSTRUCTION));  // open: sel
  IF_ID if_id_1 (
    .Data(INSTRUCTION), .ENABLE(1'b1), .CLK(MAIN_CLK_out),
    .Output({if_id_1_output[19:12], if_id_1_output_2, if_id_1_output[7:0]}));
  Clock MAIN_CLK (.out(MAIN_CLK_out));
  Multiplexer #(.disabled(0), .enable("false")) multiplexer_1 (
    .in0(MAIN_CLK_out), .in1(clock_1_out), .out(multiplexer_1_out), .sel(Reg_Write_Manual));
  Control_Unit control_unit_1 (
    .INSTRUCTION(if_id_1_output[19:16]), .ALU_OP_0(control_unit_1_alu_op_0[0]),
    .ALU_OP_1(control_unit_1_alu_op_0[1]), .ALU_OP_2(control_unit_1_alu_op_0[2]),
    .MEM_WRITE(control_unit_1_mem_write), .MEM_READ(control_unit_1_mem_read),
    .REG_WRITE(control_unit_1_alu_op_0[3]));  // open: JMP, BRANCH, MEM_2_REG, ALU_SRC, REG_DEST, SHIFT, Branch_N
  Registers registers_1 (
    .READ_REGISTER_1(if_id_1_output[15:12]), .READ_REGISTER_2(if_id_1_output_2), .WRITE_REGISTER(WR_3),
    .WRITE_DATA(WD), .REG_WRITE(multiplexer_4_out), .READ_DATA_1(registers_1_read_data_1),
    .READ_DATA_2(registers_1_read_data_2), .CLK(multiplexer_1_out), .t0(t0), .t1(t1), .t2(t2), .t3(t3),
    .t4(t4), .zero(zero), .sp(sp), .t5(t5));
  ID_EX id_ex_1 (
    .CNTRL(control_unit_1_alu_op_0), .RD1(registers_1_read_data_1), .RD2(registers_1_read_data_2),
    .CLK(MAIN_CLK_out), .CNTRL_OUT(id_ex_1_cntrl_out), .RD1_2(id_ex_1_rd1_2), .RD1_3(id_ex_1_rd1_3),
    .ENABLE(1'b1), .WR(if_id_1_output[7:4]), .WR_2(id_ex_1_wr_2), .Rd(if_id_1_output[15:12]),
    .Rs(if_id_1_output_2), .Rd_2(id_ex_1_rd_2), .Rs_2(id_ex_1_rs_2), .MW(control_unit_1_mem_write),
    .MW_2(id_ex_1_mw_2), .MR(control_unit_1_mem_read), .MR_2(id_ex_1_mr_2));
  Multiplexer #(.select(2), .width(8), .disabled(0), .enable("false")) multiplexer_2 (
    .in0(id_ex_1_rd1_3), .in1(alu3), .in2(alu2), .out(B), .sel(forwarding_unit_1_fd_b));  // open: in3
  Multiplexer #(.select(2), .width(8), .disabled(0), .enable("false")) multiplexer_3 (
    .in0(id_ex_1_rd1_2), .in1(alu3), .in2(alu2), .out(A), .sel(forwarding_unit_1_fd_a));  // open: in3
  Forwarding_Unit forwarding_unit_1 (
    .MEM_WB_RegWrite(mem_wb_1_rw_2), .EX_MEM_RegWrite(ex_mem_1_rw_2), .MEM_WB_RegRd(WR_2), .EX_MEM_RegRd(WR),
    .ID_EX_RegisterRs(id_ex_1_rd_2), .ID_EX_RegisterRt(id_ex_1_rs_2), .FD_A(forwarding_unit_1_fd_a),
    .FD_B(forwarding_unit_1_fd_b));
  ALU alu_1 (.A(A), .B(B), .ALUop(id_ex_1_cntrl_out[2:0]), .ZF(out_10), .F(alu1));  // open: out_5, out_4
  EX_MEM ex_mem_1 (
    .ALU(alu1), .RW(id_ex_1_cntrl_out[3]), .CLK(MAIN_CLK_out), .ENABLE(1'b1), .ALU_2(alu2),
    .RW_2(ex_mem_1_rw_2), .WR(id_ex_1_wr_2), .WR_2(WR), .MW(id_ex_1_mw_2), .MW_2(ex_mem_1_mw_2),
    .MR(id_ex_1_mr_2), .MR_2(ex_mem_1_mr_2), .RD2(id_ex_1_rd1_3), .RD2_2(ex_mem_1_rd2_2));
  Multiplexer #(.disabled(0), .enable("false")) multiplexer_4 (
    .in0(mem_wb_1_rw_2), .in1(Reg_Write_Manual), .out(multiplexer_4_out), .sel(Reg_Write_Manual));
  Multiplexer #(.width(4), .disabled(0), .enable("false")) multiplexer_5 (
    .in0(WR_2), .in1(WRITE_REG_ADDRESS_MANUAL), .out(WR_3), .sel(Reg_Write_Manual));
  Multiplexer #(.width(8), .disabled(0), .enable("false")) multiplexer_6 (
    .in0(alu3), .in1(WRITE_REGISTER_DATA), .out(WD), .sel(Reg_Write_Manual));
  Data_Memory data_memory_1 (
    .WRITE_DATA(ex_mem_1_rd2_2), .MEM_WRITE(ex_mem_1_mw_2), .ADDRESS(alu2), .CLK(MAIN_CLK_out),
    .READ_DATA(data_memory_1_read_data), .MEM_READ(ex_mem_1_mr_2));
  MEM_WB mem_wb_1 (
    .ALU(alu2), .RW(ex_mem_1_rw_2), .WR(WR), .CLK(MAIN_CLK_out), .ENABLE(1'b1), .ALU_2(alu3),
    .RW_2(mem_wb_1_rw_2), .WR_2(WR_2), .RD(data_memory_1_read_data));  // open: RD_2
  Clock clock_1 (.out(clock_1_out));

  // Notes on the sheet:
  //   READ ADDRESS
  //   contents of rom_1 (hex, n*v repeats v):
  //   f56ff 10010 10220 12330 12430 13100
endmodule

module ALU (
  input  [7:0] A,
  input  [7:0] B,
  input  [2:0] ALUop,
  output out_4,
  output out_5,
  output ZF,
  output [7:0] F
);

  wire [7:0] adder_1_out, and_1_out, nor_1_out, or_1_out, subtractor_1_out;
  wire [15:0] shifter_1_out, shifter_2_out;

  Adder adder_1 (.a(A), .b(B), .out(adder_1_out), .cin(1'b0), .cout(out_4));
  Subtractor subtractor_1 (.a(A), .b(B), .out(subtractor_1_out), .bin(1'b0), .bout(out_5));
  assign or_1_out = A | B;  // OR_Gate or_1, 8 bits wide
  assign and_1_out = A & B;  // AND_Gate and_1, 8 bits wide
  assign nor_1_out = ~(A | B);  // NOR_Gate nor_1, 8 bits wide
  Shifter #(.width(16)) shifter_1 (.in({{8{1'b0}}, A}), .\dist (B[3:0]), .out(shifter_1_out));
  Shifter #(.width(16), .shift("lr")) shifter_2 (.in({{8{1'b0}}, A}), .\dist (B[3:0]), .out(shifter_2_out));
  Multiplexer #(.select(3), .width(8), .enable("false")) multiplexer_1 (
    .in0(adder_1_out), .in1(subtractor_1_out), .in2(or_1_out), .in3(and_1_out), .in4(nor_1_out),
    .in5(shifter_1_out[7:0]), .in6(shifter_2_out[7:0]), .in7({8{1'b0}}), .out(F), .sel(ALUop));
  nor nor_2 (ZF, F[0], F[1], F[2], F[3], F[4], F[5], F[6], F[7]);
endmodule

module Registers (
  input  [3:0] READ_REGISTER_1,
  input  [3:0] READ_REGISTER_2,
  input  [3:0] WRITE_REGISTER,
  input  [7:0] WRITE_DATA,
  input  CLK,
  input  REG_WRITE,
  output [7:0] t0,
  output [7:0] t1,
  output [7:0] t2,
  output [7:0] READ_DATA_1,
  output [7:0] t3,
  output [7:0] t4,
  output [7:0] zero,
  output [7:0] sp,
  output [7:0] t5,
  output [7:0] READ_DATA_2
);

  wire demultiplexer_1_out0, demultiplexer_1_out1, demultiplexer_1_out2, demultiplexer_1_out3,
       demultiplexer_1_out4, demultiplexer_1_out5, demultiplexer_1_out6, demultiplexer_1_out7;

  Demultiplexer #(.select(4), .disabled(0)) demultiplexer_1 (
    .out0(demultiplexer_1_out0), .out1(demultiplexer_1_out1), .out2(demultiplexer_1_out2),
    .out3(demultiplexer_1_out3), .out4(demultiplexer_1_out4), .out5(demultiplexer_1_out5),
    .out6(demultiplexer_1_out6), .out7(demultiplexer_1_out7), .in(1'b1), .sel(WRITE_REGISTER), .en(REG_WRITE));  // open: out8, out9, out10, out11, out12, out13, out14, out15
  Register #(.trigger("falling")) u_t0 (.D(WRITE_DATA), .en(demultiplexer_1_out0), .Q(t0), .clk(CLK));  // open: clr
  Register #(.trigger("falling")) u_t1 (.D(WRITE_DATA), .en(demultiplexer_1_out1), .Q(t1), .clk(CLK));  // open: clr
  Register #(.trigger("falling")) u_t2 (.D(WRITE_DATA), .en(demultiplexer_1_out2), .Q(t2), .clk(CLK));  // open: clr
  Register #(.trigger("falling")) u_t3 (.D(WRITE_DATA), .en(demultiplexer_1_out3), .Q(t3), .clk(CLK));  // open: clr
  Register #(.trigger("falling")) u_t4 (.D(WRITE_DATA), .en(demultiplexer_1_out4), .Q(t4), .clk(CLK));  // open: clr
  Register #(.trigger("falling")) u_ZERO (.D(WRITE_DATA), .en(demultiplexer_1_out5), .Q(zero));  // open: clk, clr
  Register #(.trigger("falling")) u_SP (.D(WRITE_DATA), .en(demultiplexer_1_out6), .Q(sp), .clk(CLK));  // open: clr
  Register #(.trigger("falling")) u_t5 (.D(WRITE_DATA), .en(demultiplexer_1_out7), .Q(t5), .clk(CLK));  // open: clr
  Multiplexer #(.select(4), .width(8), .enable("false")) multiplexer_1 (
    .in0(t0), .in1(t1), .in2(t2), .in3(t3), .in4(t4), .in5(zero), .in6(sp), .in7(t5), .out(READ_DATA_1),
    .sel(READ_REGISTER_1));  // open: in8, in9, in10, in11, in12, in13, in14, in15
  Multiplexer #(.select(4), .width(8), .enable("false")) multiplexer_2 (
    .in0(t0), .in1(t1), .in2(t2), .in3(t3), .in4(t4), .in5(zero), .in6(sp), .in7(t5), .out(READ_DATA_2),
    .sel(READ_REGISTER_2));  // open: in8, in9, in10, in11, in12, in13, in14, in15
endmodule

module Data_Memory (
  input  [7:0] ADDRESS,
  input  [7:0] WRITE_DATA,
  input  MEM_WRITE,
  input  MEM_READ,
  input  CLK,
  output [7:0] READ_DATA
);

  RAM #(.bus("separate")) ram_1 (
    .addr(ADDRESS), .din(WRITE_DATA), .data(READ_DATA), .str(MEM_WRITE), .clk(CLK), .ld(MEM_READ));  // open: sel, clr

  // Notes on the sheet:
  //   DATA MEMORY
endmodule

module Control_Unit (
  input  [3:0] INSTRUCTION,
  output ALU_OP_0,
  output ALU_OP_1,
  output ALU_OP_2,
  output JMP,
  output BRANCH,
  output MEM_WRITE,
  output MEM_READ,
  output REG_WRITE,
  output MEM_2_REG,
  output ALU_SRC,
  output REG_DEST,
  output SHIFT,
  output Branch_N
);

  wire [15:15] rom_1_data;

  ROM #(.addrWidth(4), .dataWidth(16)) rom_1 (
    .addr(INSTRUCTION),
    .data({{3{rom_1_data[15]}}, Branch_N, SHIFT, REG_DEST, ALU_SRC, MEM_2_REG, REG_WRITE, MEM_READ, MEM_WRITE, BRANCH, JMP, ALU_OP_2, ALU_OP_1, ALU_OP_0}));  // open: sel
  // also tied to GND on the sheet: rom_1_data[15]

  // Notes on the sheet:
  //   contents of rom_1 (hex, n*v repeats v):
  //   71f 480 482 e85 283 1501 483 282 e86 511 3c0 281 481 720 484 280
endmodule

module IF_ID (
  input  [19:0] Data,
  input  ENABLE,
  input  CLK,
  output [19:0] Output
);

  Register #(.width(20)) register_1 (.D(Data), .en(ENABLE), .Q(Output), .clk(CLK));  // open: clr
endmodule

module ID_EX (
  input  [3:0] CNTRL,
  input  [7:0] RD1,
  input  [7:0] RD2,
  input  [3:0] WR,
  input  [3:0] Rd,
  input  [3:0] Rs,
  input  MW,
  input  MR,
  input  CLK,
  input  ENABLE,
  output [3:0] CNTRL_OUT,
  output [7:0] RD1_2,
  output [7:0] RD1_3,
  output [3:0] WR_2,
  output [3:0] Rd_2,
  output [3:0] Rs_2,
  output MW_2,
  output MR_2
);

  Register #(.width(4)) _4_bit (.D(CNTRL), .en(ENABLE), .Q(CNTRL_OUT), .clk(CLK));  // open: clr
  Register _8_bit (.D(RD1), .en(ENABLE), .Q(RD1_2), .clk(CLK));  // open: clr
  Register _8_bit_2 (.D(RD2), .en(ENABLE), .Q(RD1_3), .clk(CLK));  // open: clr
  Register #(.width(4)) _4_bit_2 (.D(WR), .en(ENABLE), .Q(WR_2), .clk(CLK));  // open: clr
  Register #(.width(4)) _4_bit_3 (.D(Rd), .en(ENABLE), .Q(Rd_2), .clk(CLK));  // open: clr
  Register #(.width(4)) _4_bit_4 (.D(Rs), .en(ENABLE), .Q(Rs_2), .clk(CLK));  // open: clr
  Register #(.width(1)) _1_bit (.D(MW), .en(ENABLE), .Q(MW_2), .clk(CLK));  // open: clr
  Register #(.width(1)) _1_bit_2 (.D(MR), .en(ENABLE), .Q(MR_2), .clk(CLK));  // open: clr
endmodule

module EX_MEM (
  input  [7:0] ALU,
  input  RW,
  input  [3:0] WR,
  input  MW,
  input  MR,
  input  [7:0] RD2,
  input  CLK,
  input  ENABLE,
  output [7:0] ALU_2,
  output RW_2,
  output [3:0] WR_2,
  output MW_2,
  output MR_2,
  output [7:0] RD2_2
);

  Register u_ALU (.D(ALU), .en(ENABLE), .Q(ALU_2), .clk(CLK));  // open: clr
  Register #(.width(1)) u_RW (.D(RW), .en(ENABLE), .Q(RW_2), .clk(CLK));  // open: clr
  Register #(.width(4)) u_WR (.D(WR), .en(ENABLE), .Q(WR_2), .clk(CLK));  // open: clr
  Register #(.width(1)) u_MW (.D(MW), .en(ENABLE), .Q(MW_2), .clk(CLK));  // open: clr
  Register #(.width(1)) u_MR (.D(MR), .en(ENABLE), .Q(MR_2), .clk(CLK));  // open: clr
  Register u_RD2 (.D(RD2), .en(ENABLE), .Q(RD2_2), .clk(CLK));  // open: clr
endmodule

module MEM_WB (
  input  [7:0] ALU,
  input  RW,
  input  [3:0] WR,
  input  [7:0] RD,
  input  CLK,
  input  ENABLE,
  output [7:0] ALU_2,
  output RW_2,
  output [3:0] WR_2,
  output [7:0] RD_2
);

  Register u_ALU (.D(ALU), .en(ENABLE), .Q(ALU_2), .clk(CLK));  // open: clr
  Register #(.width(1)) u_RW (.D(RW), .en(ENABLE), .Q(RW_2), .clk(CLK));  // open: clr
  Register #(.width(4)) u_WR (.D(WR), .en(ENABLE), .Q(WR_2), .clk(CLK));  // open: clr
  Register u_RD (.D(RD), .en(ENABLE), .Q(RD_2), .clk(CLK));  // open: clr
endmodule

module Forwarding_Unit (
  input  MEM_WB_RegWrite,
  input  EX_MEM_RegWrite,
  input  [3:0] MEM_WB_RegRd,
  input  [3:0] EX_MEM_RegRd,
  input  [3:0] ID_EX_RegisterRs,
  input  [3:0] ID_EX_RegisterRt,
  output [1:0] FD_A,
  output [1:0] FD_B
);

  wire comparator_1_eq, comparator_2_eq, comparator_3_eq, comparator_4_eq, comparator_5_eq, comparator_6_eq,
       nand_1_out, nand_2_out, not_1_out, not_2_out;
  wire [1:0] and_1_out, and_3_out;

  Comparator #(.width(4)) comparator_1 (.a(MEM_WB_RegRd), .b(4'b0101), .eq(comparator_1_eq));  // open: gt, lt
  Comparator #(.width(4)) comparator_2 (.a(EX_MEM_RegRd), .b(4'b0101), .eq(comparator_2_eq));  // open: gt, lt
  Comparator #(.width(4)) comparator_3 (.a(EX_MEM_RegRd), .b(ID_EX_RegisterRs), .eq(comparator_3_eq));  // open: gt, lt
  Comparator #(.width(4)) comparator_4 (.a(MEM_WB_RegRd), .b(ID_EX_RegisterRs), .eq(comparator_4_eq));  // open: gt, lt
  Comparator #(.width(4)) comparator_5 (.a(EX_MEM_RegRd), .b(ID_EX_RegisterRt), .eq(comparator_5_eq));  // open: gt, lt
  Comparator #(.width(4)) comparator_6 (.a(MEM_WB_RegRd), .b(ID_EX_RegisterRt), .eq(comparator_6_eq));  // open: gt, lt
  not not_1 (not_1_out, comparator_1_eq);
  not not_2 (not_2_out, comparator_2_eq);
  // NOT_Gate not_3 has open pins: in=comparator_3_eq, out=open
  nand nand_1 (nand_1_out, not_2_out, EX_MEM_RegWrite, comparator_3_eq);
  and and_1 (and_1_out[0], nand_1_out, MEM_WB_RegWrite, not_1_out, comparator_4_eq);
  and and_2 (and_1_out[1], EX_MEM_RegWrite, not_2_out, comparator_3_eq);
  nand nand_2 (nand_2_out, EX_MEM_RegWrite, not_2_out, comparator_5_eq);
  and and_3 (and_3_out[0], nand_2_out, MEM_WB_RegWrite, not_1_out, comparator_6_eq);
  and and_4 (and_3_out[1], EX_MEM_RegWrite, not_1_out, comparator_5_eq);
  Multiplexer #(.select(2), .width(2), .disabled(0), .enable("false")) multiplexer_1 (
    .in0(2'b00), .in1(2'b01), .in2(2'b10), .in3(2'b01), .out(FD_A), .sel(and_1_out));
  Multiplexer #(.select(2), .width(2), .disabled(0), .enable("false")) multiplexer_2 (
    .in0(2'b00), .in1(2'b01), .in2(2'b10), .in3(2'b01), .out(FD_B), .sel(and_3_out));

  // Notes on the sheet:
  //   EX/MEM.RegisterRd = ID/EX.RegisterRs
  //   MEM/WB.RegisterRd = ID/EX.RegisterRs
  //   EX/MEM.RegisterRD = ID/EX.RegisterRt
  //   MEM/WB.RegisterRd = ID/EX.RegisterRt
  //   MEM/WB.RegisterRd ≠ 101
  //   EX/MEM.RegRd ≠ 101
endmodule
